# Fritzing sketch hxsMidiSwitchTouch-shield (saved by Fritzing 0.9.4)
stripboards: 1

parts:
  MIDI_TX = MIDI_CONN_FEMALE [package=din_5_female]
  TRS_jack_to_expression_pedal = Audio Jack Breakout
  Nextion_screen = double row female pin header, 4 pins [form="♀ (female)"]
  S17 = Pushbutton [package="[THT]"]
  S18 = Pushbutton [package="[THT]"]
  S19 = Pushbutton [package="[THT]"]
  S20 = Pushbutton [package="[THT]"]
  S21 = Pushbutton [package="[THT]"]
  S22 = Pushbutton [package="[THT]"]
  S23 = Pushbutton [package="[THT]"]
  S24 = Pushbutton [package="[THT]"]
  R1_-TS_pulldown = Resistor [tolerance=±5% resistance=10k package=THT]
  R2_-_V_div_known = Resistor [tolerance=±5% resistance=100k package=THT]
  R3_(MIDI_TX) = Resistor [tolerance=±5% resistance=220 package=THT]
  Part4 = Arduino Mega 2560 (Rev3)  # not connected
  Crybaby_instrument_jack = Audio Jack Breakout
  Crybaby_PCB_header = female pin header, 8 pins [form="♀ (female)"]
  R4_-_Crybaby_pedal_pot1 = Rotary Potentiometer (Small) [maximum_resistance=100kΩ package=THT]
  Crybaby_harness_plug = female pin header, 8 pins [form="♀ (female)"]
  Crybaby_toeswitch = Toggle Switch [package=THT]
  Crybaby_9V_battery_clip = Battery Holders [package=battery]

nets:
  N1: MIDI_TX.NC1, Nextion_screen.pin1, S17.Pin_1, S17.Pin_2, S18.Pin_1, S18.Pin_2, S19.Pin_1, S19.Pin_2, S20.Pin_1, S20.Pin_2, S21.Pin_1, S21.Pin_2, S22.Pin_1, S22.Pin_2, S23.Pin_1, S24.Pin_1, S24.Pin_2, R2_-_V_div_known.Pin_0
  N2: MIDI_TX.MIDI_IN, R3_(MIDI_TX).Pin_1
  N3: MIDI_TX.MIDI_OUT, TRS_jack_to_expression_pedal.GND, Nextion_screen.pin4, R1_-TS_pulldown.Pin_0
  N4: TRS_jack_to_expression_pedal.RING, R1_-TS_pulldown.Pin_1
  N5: TRS_jack_to_expression_pedal.TIP, R2_-_V_div_known.Pin_1
  N6: S19.Pin_3, S19.Pin_4, S20.Pin_3, S20.Pin_4, S21.Pin_4
  N7: S22.Pin_3, S22.Pin_4, S23.Pin_3, S23.Pin_4
  N8: Crybaby_instrument_jack.GND, Crybaby_PCB_header.pin3, R4_-_Crybaby_pedal_pot1.leg2, Crybaby_harness_plug.pin6, Crybaby_toeswitch.L1
  N9: Crybaby_instrument_jack.RING, Crybaby_PCB_header.pin1, Crybaby_harness_plug.pin7, Crybaby_toeswitch.L2
  N10: Crybaby_instrument_jack.TIP, Crybaby_PCB_header.pin4, R4_-_Crybaby_pedal_pot1.wiper, Crybaby_harness_plug.pin5
  N11: R4_-_Crybaby_pedal_pot1.leg1, Crybaby_harness_plug.pin3
  N12: Crybaby_harness_plug.pin1, Crybaby_9V_battery_clip.-
  N13: Crybaby_harness_plug.pin2, Crybaby_9V_battery_clip.+
  N14: Crybaby_harness_plug.pin4, Crybaby_toeswitch.COM

notes:
  Line 6 / Mission default TRS EXP/switch config :
  EXP: tip (yellow in CB)
  FS: ring (purple in CB)
  ??: sleeve (+5v?) (blue)
